# Fritzing sketch GPIO Switches (saved by Fritzing 0.9.3b)
breadboards: 1

parts:
  R1 = Resistor [tolerance=±5% resistance=4.7k package=THT]
  Raspberry_Pi1 = Raspberry Pi 2
  S1 = Momentary Switch [package=ksa_sealed_tac_switch]
  S2 = Momentary Switch [package=ksa_sealed_tac_switch]
  Q2 = MOSFET-NCHANNEL [package=to220v]

nets:
  N1: R1.Pin_0, Raspberry_Pi1.GPIO25, Q2.G
  N2: R1.Pin_1, S1.1, S2.1, Q2.S
  N3: Raspberry_Pi1.GND, S1.2
  N4: Raspberry_Pi1.GPIO24, S1.4
  N5: Raspberry_Pi1.GPIO23, S2.4
